# Fritzing sketch lateralAccelerator (saved by Fritzing 0.9.2b)

parts:
  부품1 = Arduino Nano (Rev3.0)
  LED2 = RGB LED (com. cathode, rgb) [package="5 mm [THT]"]
  LED17 = smd LED [color="Red (633nm)" package="1206 [SMD]"]
  LED18 = smd LED [color="Red (633nm)" package="1206 [SMD]"]
  LED25 = smd LED [color="Red (633nm)" package="1206 [SMD]"]
  LED26 = smd LED [color="Red (633nm)" package="1206 [SMD]"]
  LED27 = smd LED [color="Red (633nm)" package="1206 [SMD]"]
  LED28 = smd LED [color="Red (633nm)" package="1206 [SMD]"]
  LED29 = smd LED [color="Red (633nm)" package="1206 [SMD]"]
  LED30 = smd LED [color="Red (633nm)" package="1206 [SMD]"]
  LED31 = smd LED [color="Red (633nm)" package="1206 [SMD]"]
  LED32 = smd LED [color="Red (633nm)" package="1206 [SMD]"]
  GY2 = MPU-6050 Board GY-521 [form="♀ (female)" package=THT]

nets:
  N1: 부품1.GND, LED2.common_cathode, LED17.cathode, LED18.cathode, LED25.cathode, LED26.cathode, LED27.cathode, LED28.cathode, LED29.cathode, LED30.cathode, LED31.cathode, LED32.cathode, GY2.pin2
  N2: 부품1.D2, LED32.anode
  N3: 부품1.D3, LED31.anode
  N4: 부품1.D4, LED30.anode
  N5: 부품1.D5, LED2.blue_anode
  N6: 부품1.D6, LED2.red_anode
  N7: 부품1.D7, LED29.anode
  N8: 부품1.D8, LED17.anode
  N9: 부품1.D9, LED18.anode
  N10: 부품1.D10, LED26.anode
  N11: 부품1.D11/MOSI, LED28.anode
  N12: 부품1.D12/MISO, LED27.anode
  N13: 부품1.5V, GY2.pin1
  N14: 부품1.A5, GY2.pin3
  N15: 부품1.A4, GY2.pin4
  N16: 부품1.D13/SCK, LED25.anode

custom parts:
  MPU-6050 Board GY-521: Acelerometro y Giroscopio MPU-6050 Board GY-521
